// Logisim project cast.circ as structural Verilog: 2 circuits, main circuit sign2two4
module sign2two4 (
  input  [3:0] A,
  output [3:0] out_2
);

  wire full_adder_1_p4, full_adder_2_p4, xor_1_out, xor_2_out, xor_3_out;

  xor xor_1 (xor_1_out, A[0], A[3]);
  xor xor_2 (xor_2_out, A[1], A[3]);
  xor xor_3 (xor_3_out, A[2], A[3]);
  // full_adder full_adder_1: pin names not known; wires that end beside it: xor_1_out, 1'b0, A[3], full_adder_1_p4, out_2[0]
  // full_adder full_adder_2: pin names not known; wires that end beside it: xor_2_out, 1'b0, full_adder_1_p4, full_adder_2_p4, out_2[1]
  // full_adder full_adder_3: pin names not known; wires that end beside it: xor_3_out, 1'b0, full_adder_2_p4, out_2[2]
  // NoConnect on nothing

  assign out_2[3] = A[3];
endmodule

module two2sign4 (
  input  [3:0] A,
  output [3:0] out_2
);

  wire full_adder_1_p4, full_adder_1_p5, full_adder_2_p4, full_adder_2_p5, full_adder_3_p4;

  // NoConnect on nothing
  // full_adder full_adder_1: pin names not known; wires that end beside it: A[0], A[3], 1'b0, full_adder_1_p4, full_adder_1_p5
  // full_adder full_adder_2: pin names not known; wires that end beside it: A[1], A[3], full_adder_1_p4, full_adder_2_p4, full_adder_2_p5
  // full_adder full_adder_3: pin names not known; wires that end beside it: A[2], A[3], full_adder_2_p4, full_adder_3_p4
  xor xor_1 (out_2[0], full_adder_1_p5, A[3]);
  xor xor_2 (out_2[1], full_adder_2_p5, A[3]);
  xor xor_3 (out_2[2], full_adder_3_p4, A[3]);

  assign out_2[3] = A[3];
endmodule
