// Logisim project display_int.circ as structural Verilog: 1 circuit, main circuit main
module main (
  input  A,
  input  B,
  input  C,
  input  D,
  output S,
  output H0,
  output H1,
  output H2,
  output H3,
  output H4,
  output H5,
  output H6
);

  wire and_1_out, and_2_out, and_3_out, and_4_out, and_5_out, and_6_out, and_7_out, and_8_out, and_9_out,
       and_10_out, and_11_out, and_12_out, and_13_out, and_14_out, and_15_out, and_16_out, not_1_out,
       not_2_out, not_3_out;

  not not_1 (not_1_out, B);
  not not_2 (not_2_out, C);
  not not_3 (not_3_out, D);
  and and_1 (and_1_out, B, D);
  and and_2 (and_2_out, not_1_out, not_3_out);
  and and_3 (and_3_out, not_3_out, not_2_out);
  and and_4 (and_4_out, D, C);
  and and_5 (and_5_out, D, not_2_out, B);
  and and_6 (and_6_out, not_3_out, not_1_out);
  and and_7 (and_7_out, C, not_3_out);
  and and_8 (and_8_out, C, not_1_out);
  and and_9 (and_9_out, not_1_out, not_3_out);
  and and_10 (and_10_out, C, not_3_out);
  and and_11 (and_11_out, not_3_out, not_2_out);
  and and_12 (and_12_out, not_2_out, B);
  and and_13 (and_13_out, not_3_out, B);
  and and_14 (and_14_out, C, not_1_out);
  and and_15 (and_15_out, not_3_out, C);
  and and_16 (and_16_out, not_2_out, B);
  or or_1 (H0, C, and_1_out, and_2_out);
  or or_2 (H1, and_3_out, not_1_out, and_4_out);
  or or_3 (H2, D, not_2_out, B);
  or or_4 (H3, and_5_out, and_6_out, and_7_out, and_8_out);
  or or_5 (H5, and_11_out, and_12_out, and_13_out);
  or or_6 (H4, and_9_out, and_10_out);
  or or_7 (H6, and_14_out, and_15_out, and_16_out);

  assign S = A;
endmodule
